// Logisim project control-logic.circ as structural Verilog: 1 circuit, main circuit control_logic
module control_logic (
  input  [31:0] Instruction,
  input  BrEq,
  input  BrLt,
  output PCSel,
  output RegWEn,
  output [2:0] ImmSel,
  output BrUn,
  output ASel,
  output BSel,
  output [3:0] ALUSel,
  output MemWEn,
  output [1:0] WBSel
);

  wire add0, addi, and0, and_18_out, and_19_out, and_20_out, and_36_out, and_37_out, and_38_out, andi, auipc,
       B, beq, bge, bgeu, blt, bltu, bne, comparator_10_eq, comparator_11_eq, comparator_12_eq,
       comparator_13_eq, comparator_14_eq, comparator_15_eq, comparator_16_eq, comparator_17_eq,
       comparator_18_eq, comparator_19_eq, comparator_20_eq, comparator_21_eq, comparator_22_eq,
       comparator_23_eq, comparator_24_eq, comparator_25_eq, comparator_26_eq, comparator_27_eq,
       comparator_28_eq, comparator_29_eq, comparator_30_eq, comparator_31_eq, comparator_32_eq,
       comparator_33_eq, comparator_34_eq, comparator_35_eq, comparator_36_eq, comparator_37_eq,
       comparator_38_eq, comparator_39_eq, comparator_40_eq, comparator_41_eq, comparator_42_eq,
       comparator_43_eq, comparator_44_eq, comparator_45_eq, comparator_46_eq, comparator_47_eq,
       comparator_48_eq, comparator_49_eq, comparator_50_eq, comparator_51_eq, comparator_52_eq,
       comparator_53_eq, comparator_54_eq, comparator_55_eq, comparator_56_eq, I1, I2, jal, jalr, lb, lh,
       lui, lw, mul0, mulh0, mulhu0, not_1_out, not_2_out, or0, or_1_out, or_2_out, or_3_out, or_4_out, ori,
       R, S, sb, sh, sll0, slli, slt0, slti, sra0, srai, srl0, srli, sub0, sw, xor0, xori;
  wire [5:0] ROMinput;
  wire [15:14] rom_1_data;

  ROM #(.addrWidth(6), .dataWidth(16)) rom_1 (
    .addr(ROMinput), .data({rom_1_data, WBSel, MemWEn, ALUSel, BSel, ASel, BrUn, ImmSel, RegWEn}));
  Comparator #(.width(7)) comparator_1 (.a(Instruction[6:0]), .b(7'b0110011), .eq(R));  // open: gt, lt
  Comparator #(.width(7)) comparator_2 (.a(Instruction[6:0]), .b(7'b0000011), .eq(I1));  // open: gt, lt
  Comparator #(.width(7)) comparator_3 (.a(Instruction[6:0]), .b(7'b0010011), .eq(I2));  // open: gt, lt
  Comparator #(.width(7)) comparator_4 (.a(Instruction[6:0]), .b(7'b0100011), .eq(S));  // open: gt, lt
  Comparator #(.width(7)) comparator_5 (.a(Instruction[6:0]), .b(7'b1100011), .eq(B));  // open: gt, lt
  Comparator #(.width(7)) comparator_6 (.a(Instruction[6:0]), .b(7'b0010111), .eq(auipc));  // open: gt, lt
  Comparator #(.width(7)) comparator_7 (.a(Instruction[6:0]), .b(7'b0110111), .eq(lui));  // open: gt, lt
  Comparator #(.width(7)) comparator_8 (.a(Instruction[6:0]), .b(7'b1101111), .eq(jal));  // open: gt, lt
  Comparator #(.width(7)) comparator_9 (.a(Instruction[6:0]), .b(7'b1100111), .eq(jalr));  // open: gt, lt
  Comparator #(.mode("unsigned"), .width(3)) comparator_10 (
    .a(Instruction[14:12]), .b(3'b000), .eq(comparator_10_eq));  // open: gt, lt
  Comparator #(.mode("unsigned"), .width(7)) comparator_11 (
    .a(Instruction[31:25]), .b({7{1'b0}}), .eq(comparator_11_eq));  // open: gt, lt
  Comparator #(.mode("unsigned"), .width(3)) comparator_12 (
    .a(Instruction[14:12]), .b(3'b000), .eq(comparator_12_eq));  // open: gt, lt
  Comparator #(.mode("unsigned"), .width(7)) comparator_13 (
    .a(Instruction[31:25]), .b(7'b0000001), .eq(comparator_13_eq));  // open: gt, lt
  Comparator #(.mode("unsigned"), .width(3)) comparator_14 (
    .a(Instruction[14:12]), .b(3'b000), .eq(comparator_14_eq));  // open: gt, lt
  Comparator #(.mode("unsigned"), .width(7)) comparator_15 (
    .a(Instruction[31:25]), .b(7'b0100000), .eq(comparator_15_eq));  // open: gt, lt
  Comparator #(.mode("unsigned"), .width(3)) comparator_16 (
    .a(Instruction[14:12]), .b(3'b001), .eq(comparator_16_eq));  // open: gt, lt
  Comparator #(.mode("unsigned"), .width(7)) comparator_17 (
    .a(Instruction[31:25]), .b({7{1'b0}}), .eq(comparator_17_eq));  // open: gt, lt
  Comparator #(.mode("unsigned"), .width(3)) comparator_18 (
    .a(Instruction[14:12]), .b(3'b001), .eq(comparator_18_eq));  // open: gt, lt
  Comparator #(.mode("unsigned"), .width(7)) comparator_19 (
    .a(Instruction[31:25]), .b(7'b0000001), .eq(comparator_19_eq));  // open: gt, lt
  Comparator #(.mode("unsigned"), .width(3)) comparator_20 (
    .a(Instruction[14:12]), .b(3'b011), .eq(comparator_20_eq));  // open: gt, lt
  Comparator #(.mode("unsigned"), .width(7)) comparator_21 (
    .a(Instruction[31:25]), .b(7'b0000001), .eq(comparator_21_eq));  // open: gt, lt
  Comparator #(.mode("unsigned"), .width(3)) comparator_22 (
    .a(Instruction[14:12]), .b(3'b000), .eq(comparator_22_eq));  // open: gt, lt
  Comparator #(.mode("unsigned"), .width(3)) comparator_23 (
    .a(Instruction[14:12]), .b(3'b001), .eq(comparator_23_eq));  // open: gt, lt
  Comparator #(.mode("unsigned"), .width(7)) comparator_24 (
    .a(Instruction[31:25]), .b({7{1'b0}}), .eq(comparator_24_eq));  // open: gt, lt
  Comparator #(.mode("unsigned"), .width(3)) comparator_25 (
    .a(Instruction[14:12]), .b(3'b010), .eq(comparator_25_eq));  // open: gt, lt
  Comparator #(.mode("unsigned"), .width(3)) comparator_26 (
    .a(Instruction[14:12]), .b(3'b100), .eq(comparator_26_eq));  // open: gt, lt
  Comparator #(.mode("unsigned"), .width(3)) comparator_27 (
    .a(Instruction[14:12]), .b(3'b101), .eq(comparator_27_eq));  // open: gt, lt
  Comparator #(.mode("unsigned"), .width(7)) comparator_28 (
    .a(Instruction[31:25]), .b({7{1'b0}}), .eq(comparator_28_eq));  // open: gt, lt
  Comparator #(.mode("unsigned"), .width(3)) comparator_29 (
    .a(Instruction[14:12]), .b(3'b101), .eq(comparator_29_eq));  // open: gt, lt
  Comparator #(.mode("unsigned"), .width(7)) comparator_30 (
    .a(Instruction[31:25]), .b(7'b0100000), .eq(comparator_30_eq));  // open: gt, lt
  Comparator #(.mode("unsigned"), .width(3)) comparator_31 (
    .a(Instruction[14:12]), .b(3'b110), .eq(comparator_31_eq));  // open: gt, lt
  Comparator #(.mode("unsigned"), .width(3)) comparator_32 (
    .a(Instruction[14:12]), .b(3'b111), .eq(comparator_32_eq));  // open: gt, lt
  Comparator #(.mode("unsigned"), .width(3)) comparator_33 (
    .a(Instruction[14:12]), .b(3'b000), .eq(comparator_33_eq));  // open: gt, lt
  Comparator #(.mode("unsigned"), .width(3)) comparator_34 (
    .a(Instruction[14:12]), .b(3'b001), .eq(comparator_34_eq));  // open: gt, lt
  Comparator #(.mode("unsigned"), .width(3)) comparator_35 (
    .a(Instruction[14:12]), .b(3'b010), .eq(comparator_35_eq));  // open: gt, lt
  and and_1 (add0, R, comparator_10_eq, comparator_11_eq);
  and and_2 (mul0, R, comparator_12_eq, comparator_13_eq);
  and and_3 (sub0, R, comparator_14_eq, comparator_15_eq);
  and and_4 (sll0, R, comparator_16_eq, comparator_17_eq);
  and and_5 (mulh0, R, comparator_18_eq, comparator_19_eq);
  and and_6 (mulhu0, R, comparator_20_eq, comparator_21_eq);
  and and_7 (lb, I1, comparator_33_eq);
  and and_8 (lh, I1, comparator_34_eq);
  and and_9 (lw, I1, comparator_35_eq);
  and and_10 (addi, I2, comparator_22_eq);
  and and_11 (slli, I2, comparator_23_eq, comparator_24_eq);
  and and_12 (slti, I2, comparator_25_eq);
  and and_13 (xori, I2, comparator_26_eq);
  and and_14 (srli, I2, comparator_27_eq, comparator_28_eq);
  and and_15 (srai, I2, comparator_29_eq, comparator_30_eq);
  and and_16 (ori, I2, comparator_31_eq);
  and and_17 (andi, I2, comparator_32_eq);
  Comparator #(.mode("unsigned"), .width(3)) comparator_36 (
    .a(Instruction[14:12]), .b(3'b010), .eq(comparator_36_eq));  // open: gt, lt
  Comparator #(.mode("unsigned"), .width(7)) comparator_37 (
    .a(Instruction[31:25]), .b({7{1'b0}}), .eq(comparator_37_eq));  // open: gt, lt
  Comparator #(.mode("unsigned"), .width(3)) comparator_38 (
    .a(Instruction[14:12]), .b(3'b100), .eq(comparator_38_eq));  // open: gt, lt
  Comparator #(.mode("unsigned"), .width(7)) comparator_39 (
    .a(Instruction[31:25]), .b({7{1'b0}}), .eq(comparator_39_eq));  // open: gt, lt
  Comparator #(.mode("unsigned"), .width(3)) comparator_40 (
    .a(Instruction[14:12]), .b(3'b101), .eq(comparator_40_eq));  // open: gt, lt
  Comparator #(.mode("unsigned"), .width(7)) comparator_41 (
    .a(Instruction[31:25]), .b({7{1'b0}}), .eq(comparator_41_eq));  // open: gt, lt
  Comparator #(.mode("unsigned"), .width(3)) comparator_42 (
    .a(Instruction[14:12]), .b(3'b101), .eq(comparator_42_eq));  // open: gt, lt
  Comparator #(.mode("unsigned"), .width(7)) comparator_43 (
    .a(Instruction[31:25]), .b(7'b0100000), .eq(comparator_43_eq));  // open: gt, lt
  Comparator #(.mode("unsigned"), .width(3)) comparator_44 (
    .a(Instruction[14:12]), .b(3'b110), .eq(comparator_44_eq));  // open: gt, lt
  Comparator #(.mode("unsigned"), .width(7)) comparator_45 (
    .a(Instruction[31:25]), .b({7{1'b0}}), .eq(comparator_45_eq));  // open: gt, lt
  Comparator #(.mode("unsigned"), .width(3)) comparator_46 (
    .a(Instruction[14:12]), .b(3'b111), .eq(comparator_46_eq));  // open: gt, lt
  Comparator #(.mode("unsigned"), .width(7)) comparator_47 (
    .a(Instruction[31:25]), .b({7{1'b0}}), .eq(comparator_47_eq));  // open: gt, lt
  Comparator #(.mode("unsigned"), .width(3)) comparator_48 (
    .a(Instruction[14:12]), .b(3'b000), .eq(comparator_48_eq));  // open: gt, lt
  Comparator #(.mode("unsigned"), .width(3)) comparator_49 (
    .a(Instruction[14:12]), .b(3'b001), .eq(comparator_49_eq));  // open: gt, lt
  Comparator #(.mode("unsigned"), .width(3)) comparator_50 (
    .a(Instruction[14:12]), .b(3'b010), .eq(comparator_50_eq));  // open: gt, lt
  Comparator #(.mode("unsigned"), .width(3)) comparator_51 (
    .a(Instruction[14:12]), .b(3'b000), .eq(comparator_51_eq));  // open: gt, lt
  Comparator #(.mode("unsigned"), .width(3)) comparator_52 (
    .a(Instruction[14:12]), .b(3'b001), .eq(comparator_52_eq));  // open: gt, lt
  Comparator #(.mode("unsigned"), .width(3)) comparator_53 (
    .a(Instruction[14:12]), .b(3'b100), .eq(comparator_53_eq));  // open: gt, lt
  Comparator #(.mode("unsigned"), .width(3)) comparator_54 (
    .a(Instruction[14:12]), .b(3'b101), .eq(comparator_54_eq));  // open: gt, lt
  Comparator #(.mode("unsigned"), .width(3)) comparator_55 (
    .a(Instruction[14:12]), .b(3'b110), .eq(comparator_55_eq));  // open: gt, lt
  Comparator #(.mode("unsigned"), .width(3)) comparator_56 (
    .a(Instruction[14:12]), .b(3'b111), .eq(comparator_56_eq));  // open: gt, lt
  not not_1 (not_1_out, BrLt);
  not not_2 (not_2_out, BrLt);
  and and_18 (and_18_out, blt, BrLt);
  and and_19 (and_19_out, bltu, BrLt);
  and and_20 (and_20_out, bne, BrEq);
  and and_21 (slt0, R, comparator_36_eq, comparator_37_eq);
  and and_22 (xor0, R, comparator_38_eq, comparator_39_eq);
  and and_23 (srl0, R, comparator_40_eq, comparator_41_eq);
  and and_24 (sra0, R, comparator_42_eq, comparator_43_eq);
  and and_25 (or0, R, comparator_44_eq, comparator_45_eq);
  and and_26 (and0, R, comparator_46_eq, comparator_47_eq);
  and and_27 (sb, S, comparator_48_eq);
  and and_28 (sh, S, comparator_49_eq);
  and and_29 (sw, S, comparator_50_eq);
  and and_30 (beq, B, comparator_51_eq);
  and and_31 (bne, B, comparator_52_eq);
  and and_32 (blt, B, comparator_53_eq);
  and and_33 (bge, B, comparator_54_eq);
  and and_34 (bltu, B, comparator_55_eq);
  and and_35 (bgeu, B, comparator_56_eq);
  and and_36 (and_36_out, beq, BrEq);
  or or_1 (or_1_out, BrEq, not_1_out);
  or or_2 (or_2_out, BrEq, not_2_out);
  and and_37 (and_37_out, bge, or_1_out);
  and and_38 (and_38_out, bgeu, or_2_out);
  or or_3 (or_3_out, and_36_out, and_37_out, and_38_out, and_18_out, and_19_out, and_20_out);
  or or_4 (or_4_out, jal, jalr);
  or or_5 (PCSel, or_3_out, or_4_out);
  Priority_Encoder #(.select_enc(6)) priority_encoder_1 (
    .in0(add0), .in1(mul0), .in2(sub0), .in3(sll0), .in4(mulh0), .in5(mulhu0), .in6(slt0), .in7(xor0),
    .in8(srl0), .in9(sra0), .in10(or0), .in11(and0), .in12(lb), .in13(lh), .in14(lw), .in15(addi),
    .in16(slli), .in17(slti), .in18(xori), .in19(srli), .in20(srai), .in21(ori), .in22(andi), .in23(sb),
    .in24(sh), .in25(sw), .in26(beq), .in27(bne), .in28(blt), .in29(bge), .in30(bltu), .in31(bgeu),
    .in32(auipc), .in33(lui), .in34(jal), .in35(jalr), .out(ROMinput));  // open: in36, in37, in38, in39, in40, in41, in42, in43, in44, in45, in46, in47, in48, in49, in50, in51, in52, in53, in54, in55, in56, in57, in58, in59, in60, in61, in62, in63, gs, en_out, en_in

  // Other names for the same wires on the sheet: opcode[6:0] = Instruction[6:0]; funct3[2:0] = Instruction[14:12];
  //   funct7[6:0] = Instruction[31:25]

  // Notes on the sheet:
  //   INPUTS to your circuit
  //   Connect ROM Input here ->
  //   contents of rom_1 (hex, n*v repeats v):
  //   1001 1401 1601 1081 1481 1581 1101 1201 1281 1681 1301 1381 841 841 841 1041 10c1 1141 1241 12c1
  //   16c1 1341 13c1 842 842 842 4*64 74 74 1067 17c7 2069 2041
  //   ROM FOR CONTROL LOGIC
  //   DON'T CHANGE THE LOCATIONS OF THE INPUTS AND OUTPUTS!
  //   This is only if you choose to do the ROM option
  //   CONNECT
  //   WIRE
  //   TO
  //   USE
  //   ROM
  //   OUTPUT from your circuit
  //   Reminder: If using ROM, use combinational logic for PCSel
endmodule
