// Logisim project imm-gen.circ as structural Verilog: 1 circuit, main circuit imm_gen
module imm_gen (
  input  [31:0] Instruction,
  input  [2:0] ImmSel,
  output [31:0] Immediate
);

  wire [31:11] I_IMM, S_IMM;
  wire [31:12] B_IMM;
  wire [31:20] J_IMM;

  assign I_IMM = {{20{Instruction[31]}}, Instruction[31]};  // Bit_Extender bit_extender_1
  assign S_IMM = {{20{Instruction[31]}}, Instruction[31]};  // Bit_Extender bit_extender_2
  assign B_IMM = {{19{Instruction[31]}}, Instruction[31]};  // Bit_Extender bit_extender_3
  assign J_IMM = {{11{Instruction[31]}}, Instruction[31]};  // Bit_Extender bit_extender_4
  Multiplexer #(.select(3), .width(32)) multiplexer_1 (
    .in0({I_IMM, Instruction[30:20]}), .in1({S_IMM, Instruction[30:25], Instruction[11:7]}),
    .in2({B_IMM, Instruction[7], Instruction[30:25], Instruction[11:8], 1'b0}),
    .in3({Instruction[31:12], {12{1'b0}}}),
    .in4({J_IMM, Instruction[19:12], Instruction[20], Instruction[30:21], 1'b0}), .out(Immediate),
    .sel(ImmSel));  // open: in5, in6, in7

  // Other names for the same wires on the sheet: B_IMM[11:1] = {Instruction[7], Instruction[30:25], Instruction[11:8]};
  //   S_IMM[10:0] = {Instruction[30:25], Instruction[11:7]}; I_IMM[10:0] = Instruction[30:20];
  //   J_IMM[19:1] = {Instruction[19:12], Instruction[20], Instruction[30:21]}; U_IMM[31:12] = Instruction[31:12]

  // Notes on the sheet:
  //   INPUTS to your circuit
  //   DON'T CHANGE THE LOCATIONS OF THE INPUTS AND OUTPUTS!
  //   OUTPUT from your circuit
endmodule
