// Logisim project partial-store.circ as structural Verilog: 1 circuit, main circuit partial_store
module partial_store (
  input  [31:0] Instruction,
  input  [31:0] MemAddress,
  input  [31:0] DataFromReg,
  input  MemWEn,
  output [3:0] MemWriteMask,
  output [31:0] DataToMem
);

  wire and_1_out, comparator_1_eq;
  wire [3:0] multiplexer_4_out, shifter_1_out;
  wire [7:0] undriven, undriven_2, undriven_3, undriven_4, undriven_5, undriven_6, undriven_7, undriven_8,
       undriven_9, undriven_10, undriven_11, undriven_12, undriven_13, undriven_14, undriven_15, undriven_16;
  wire [31:0] sb, sh;

  Multiplexer #(.select(2), .width(32)) multiplexer_1 (
    .in0({undriven_3, undriven_2, undriven, DataFromReg[7:0]}),
    .in1({undriven_6, undriven_5, DataFromReg[7:0], undriven_4}),
    .in2({undriven_11, DataFromReg[7:0], undriven_10, undriven_9}),
    .in3({DataFromReg[7:0], undriven_16, undriven_15, undriven_14}), .out(sb), .sel(MemAddress[1:0]));
  Multiplexer #(.width(32)) multiplexer_2 (
    .in0({undriven_8, undriven_7, DataFromReg[15:0]}), .in1({DataFromReg[15:0], undriven_13, undriven_12}),
    .out(sh), .sel(MemAddress[1]));
  Multiplexer #(.select(3), .width(32)) multiplexer_3 (
    .in0(sb), .in1(sh), .in2(DataFromReg), .out(DataToMem), .sel(Instruction[14:12]));  // open: in3, in4, in5, in6, in7
  Multiplexer #(.select(3), .width(4)) multiplexer_4 (
    .in0(4'b0001), .in1(4'b0011), .in2(4'b1111), .out(multiplexer_4_out), .sel(Instruction[14:12]));  // open: in3, in4, in5, in6, in7
  Shifter #(.width(4)) shifter_1 (.in(multiplexer_4_out), .\dist (MemAddress[1:0]), .out(shifter_1_out));
  Comparator #(.width(7)) comparator_1 (.a(Instruction[6:0]), .b(7'b0100011), .eq(comparator_1_eq));  // open: gt, lt
  Multiplexer #(.width(4)) multiplexer_5 (.in0(4'b0000), .in1(shifter_1_out), .out(MemWriteMask), .sel(and_1_out));
  and and_1 (and_1_out, comparator_1_eq, MemWEn);

  // Other names for the same wires on the sheet: b0[7:0] = DataFromReg[7:0]; sw[31:0] = DataFromReg;
  //   b1[7:0] = DataFromReg[15:8]; opcode[6:0] = Instruction[6:0]; rd[4:0] = Instruction[11:7];
  //   funct3[2:0] = Instruction[14:12]; rs1[4:0] = Instruction[19:15]; rs2[4:0] = Instruction[24:20];
  //   low[1:0] = MemAddress[1:0]

  // Notes on the sheet:
  //   INPUTS to your circuit
  //   DON'T CHANGE THE LOCATIONS OF THE INPUTS AND OUTPUTS!
  //   OUTPUT from your circuit
endmodule
